// Logisim project aiAlu.circ as structural Verilog
module halfAdder (
  input  a,
  input  b,
  output S,
  output C
);

  and and_1 (C, a, b);
  xor xor_1 (S, a, b);
endmodule
